# Fritzing sketch ESP32_CAM_FTDI (saved by Fritzing 0.9.3b)
circuit board: 7.08699cm x 7.04674cm

parts:
  ESP32_-_Back1 = ESP32 - CAM
  VCC1 = Battery
  U1 = ESP32-38PinWide [part_number=ESP32-38PinWide]

nets:
  N1: ESP32_-_Back1.GPIO2, ESP32_-_Back1.GPIO13
  N2: ESP32_-_Back1.GND#7, U1.GND
  5V: ESP32_-_Back1.5V, U1.VIN
  N3: ESP32_-_Back1.GPIO0, ESP32_-_Back1.GND#12
  N4: ESP32_-_Back1.3.3V_/_5V_/_P_OUT, VCC1.+
  N5: ESP32_-_Back1.GPIO3_/_RX, U1.GPIO3
  N6: ESP32_-_Back1.GPIO1_/_TX, U1.GPIO6, U1.GPIO1
  N7: ESP32_-_Back1.GND#16, VCC1.-

custom parts:
  ESP32 - CAM: The ESP32-CAM has a very competitive small-size camera module that can operate independently as a minimum system with a footprint of only 27*40.5*4.5mm and a deep sleep current of up to 6mA.
  ESP32-38PinWide: Generic 38-Pin ESP32 with wide format (only access to one side of pins on a breadboard) based on Stephen Lilley's HiLetgo ESP-WROOM-32 ESP32 ESP-32S Development Board.

// code stored in the sketch: Camera_Interfacing_ESP32.ino
#include <WiFi.h>
#include <Wire.h>
#include "esp_camera.h"

const char* ssid = "POTS2.4";
const char* password = "POTS@12340987";

WiFiServer server(80);

void setup() {
  Serial.begin(115200);
  while(!Serial){};

  WiFi.begin(ssid, password);
  while (WiFi.status() != WL_CONNECTED) {
    delay(1000);
    Serial.println("Connecting to WiFi...");
  }
  Serial.println("Connected to WiFi");

  server.begin();
  Serial.println("Server started");
  Serial.print("Use this URL to connect: ");
  Serial.print("http://");
  Serial.print(WiFi.localIP());
}

void loop() {
  WiFiClient client = server.available();
  if (!client) {
    return;
  }

  while(!client.available()){
    delay(1);
  }

  String req = client.readStringUntil('\r');
  Serial.println(req);
  client.flush();

  String s = "HTTP/1.1 200 OK\r\nContent-Type: image/jpeg\r\n\r\n";
  client.print(s);

  camera_fb_t *fb = NULL;
  fb = esp_camera_fb_get();
  if (!fb) {
    Serial.println("Camera capture failed");
    return;
  }

  client.write((uint8_t *)fb->buf, fb->len);
  esp_camera_fb_return(fb);
  Serial.println("Camera captured");
}
